// Logisim project stage1finalversion.circ as structural Verilog: 1 circuit, main circuit interface
module \interface  (
  input  in_1,
  input  in_2,
  input  in_3,
  input  in_4,
  input  in_5,
  input  in_6,
  input  in_7,
  input  in_8,
  input  in_9,
  input  in_10,
  input  in_11,
  input  in_12,
  input  in_13,
  input  in_14,
  input  in_15,
  input  in_16
);

  wire button_2_out, button_3_out;

  Button button_1 ();  // open: out
  LED led_1 ();  // open: in
  Button button_2 (.out(button_2_out));
  Button button_3 (.out(button_3_out));
  Button button_4 ();  // open: out
  Button button_5 ();  // open: out
  Button button_6 ();  // open: out
  LED led_2 ();  // open: in
  LED led_3 (.in(in_1));
  D_Flip_Flop d_ff_1 (.D(in_1), .clk(button_2_out), .reset(button_3_out));  // open: Q, Qn, preset
  LED led_4 (.in(in_2));
  LED led_5 (.in(in_3));
  D_Flip_Flop d_ff_2 (.D(in_2), .clk(button_2_out), .reset(button_3_out));  // open: Q, Qn, preset
  LED led_6 (.in(in_4));
  D_Flip_Flop d_ff_3 (.D(in_3), .clk(button_2_out), .reset(button_3_out));  // open: Q, Qn, preset
  LED led_7 (.in(in_5));
  D_Flip_Flop d_ff_4 (.D(in_4), .clk(button_2_out), .reset(button_3_out));  // open: Q, Qn, preset
  LED led_8 (.in(in_6));
  LED led_9 (.in(in_7));
  LED led_10 (.in(in_8));
  D_Flip_Flop d_ff_5 (.D(in_5), .clk(button_2_out), .reset(button_3_out));  // open: Q, Qn, preset
  D_Flip_Flop d_ff_6 (.D(in_6), .clk(button_2_out), .reset(button_3_out));  // open: Q, Qn, preset
  D_Flip_Flop d_ff_7 (.D(in_7), .clk(button_2_out), .reset(button_3_out));  // open: Q, Qn, preset
  Button button_7 ();  // open: out
  LED led_11 ();  // open: in
  D_Flip_Flop d_ff_8 (.D(button_2_out), .clk(in_8), .reset(button_3_out));  // open: Q, Qn, preset
  LED led_12 (.in(in_9));
  LED led_13 (.in(in_10));
  D_Flip_Flop d_ff_9 (.D(in_9), .clk(button_2_out), .reset(button_3_out));  // open: Q, Qn, preset
  LED led_14 (.in(in_11));
  LED led_15 (.in(in_12));
  D_Flip_Flop d_ff_10 (.D(in_10), .clk(button_2_out), .reset(button_3_out));  // open: Q, Qn, preset
  LED led_16 (.in(in_13));
  D_Flip_Flop d_ff_11 (.D(in_11), .clk(button_2_out), .reset(button_3_out));  // open: Q, Qn, preset
  LED led_17 (.in(in_14));
  D_Flip_Flop d_ff_12 (.D(in_12), .clk(button_2_out), .reset(button_3_out));  // open: Q, Qn, preset
  LED led_18 (.in(in_15));
  LED led_19 (.in(in_16));
  D_Flip_Flop d_ff_13 (.D(in_13), .clk(button_2_out), .reset(button_3_out));  // open: Q, Qn, preset
  D_Flip_Flop d_ff_14 (.D(in_14), .clk(button_2_out), .reset(button_3_out));  // open: Q, Qn, preset
  D_Flip_Flop d_ff_15 (.D(in_15), .clk(button_2_out), .reset(button_3_out));  // open: Q, Qn, preset
  D_Flip_Flop d_ff_16 (.D(in_16), .clk(button_2_out), .reset(button_3_out));  // open: Q, Qn, preset

  // Notes on the sheet:
  //   +/-
  //   +/-
  //   Load
  //   Reset 
  //   Add
  //   Subtract
  //   reset
  //   +/-
  //   Input A
  //   8 bit Binary Calculator
  //   Input A Display
  //   +/-
  //   +/-
  //   Input B
  //   Input B Display
endmodule
