// Logisim project stage2finalversion.circ as structural Verilog: 1 circuit, main circuit interface
module \interface  (
  input  in_1,
  input  in_2,
  input  in_3,
  input  in_4,
  input  in_5,
  input  in_6,
  input  in_7,
  input  in_8,
  input  in_9,
  input  in_10,
  input  in_11,
  input  in_12,
  input  in_13,
  input  in_14,
  input  in_15,
  input  in_16
);

  wire and_1_out, and_2_out, and_3_out, and_4_out, and_5_out, and_6_out, and_7_out, and_8_out, and_9_out,
       and_10_out, and_11_out, and_12_out, and_13_out, button_2_out, button_3_out, button_4_out, d_ff_1_q,
       d_ff_2_q, d_ff_3_q, d_ff_4_q, d_ff_5_q, d_ff_6_q, d_ff_7_q, d_ff_8_q, d_ff_9_q, d_ff_10_q, d_ff_11_q,
       d_ff_12_q, d_ff_13_q, d_ff_14_q, d_ff_15_q, d_ff_16_q, d_ff_17_q, d_ff_18_q, d_ff_19_q, d_ff_20_q,
       d_ff_21_q, d_ff_22_q, d_ff_23_q, d_ff_24_q, d_ff_25_q, d_ff_26_q, d_ff_27_q, d_ff_28_q, d_ff_29_q,
       d_ff_30_q, d_ff_31_q, d_ff_32_q, or_1_out, or_2_out, or_3_out, or_4_out, or_5_out, or_6_out,
       xor_1_out, xor_2_out, xor_3_out, xor_4_out, xor_5_out, xor_6_out, xor_7_out, xor_8_out, xor_9_out,
       xor_10_out, xor_11_out, xor_12_out, xor_13_out, xor_14_out, xor_15_out;

  Button button_1 ();  // open: out
  LED led_1 ();  // open: in
  Button button_2 (.out(button_2_out));
  Button button_3 (.out(button_3_out));
  Button button_4 (.out(button_4_out));
  Button button_5 ();  // open: out
  LED led_2 ();  // open: in
  xor xor_1 (xor_1_out, d_ff_2_q, d_ff_18_q);
  xor xor_2 (xor_2_out, xor_1_out, or_1_out);
  LED led_3 (.in(xor_2_out));
  LED led_4 (.in(in_1));
  D_Flip_Flop d_ff_1 (.D(in_1), .clk(button_2_out), .Q(d_ff_1_q), .reset(button_3_out));  // open: Qn, preset
  D_Flip_Flop d_ff_2 (.D(d_ff_1_q), .clk(button_4_out), .Q(d_ff_2_q), .reset(button_3_out));  // open: Qn, preset
  and and_1 (and_1_out, d_ff_4_q, d_ff_20_q);
  and and_2 (and_2_out, xor_3_out, or_2_out);
  or or_1 (or_1_out, and_1_out, and_2_out);
  LED led_5 (.in(in_2));
  LED led_6 (.in(in_3));
  D_Flip_Flop d_ff_3 (.D(in_2), .clk(button_2_out), .Q(d_ff_3_q), .reset(button_3_out));  // open: Qn, preset
  D_Flip_Flop d_ff_4 (.D(d_ff_3_q), .clk(button_4_out), .Q(d_ff_4_q), .reset(button_3_out));  // open: Qn, preset
  xor xor_3 (xor_3_out, d_ff_4_q, d_ff_20_q);
  xor xor_4 (xor_4_out, xor_3_out, or_2_out);
  LED led_7 (.in(xor_4_out));
  LED led_8 (.in(in_4));
  D_Flip_Flop d_ff_5 (.D(in_3), .clk(button_2_out), .Q(d_ff_5_q), .reset(button_3_out));  // open: Qn, preset
  D_Flip_Flop d_ff_6 (.D(d_ff_5_q), .clk(button_4_out), .Q(d_ff_6_q), .reset(button_3_out));  // open: Qn, preset
  and and_3 (and_3_out, d_ff_6_q, d_ff_22_q);
  and and_4 (and_4_out, xor_5_out, or_3_out);
  or or_2 (or_2_out, and_3_out, and_4_out);
  LED led_9 (.in(in_5));
  D_Flip_Flop d_ff_7 (.D(in_4), .clk(button_2_out), .Q(d_ff_7_q), .reset(button_3_out));  // open: Qn, preset
  D_Flip_Flop d_ff_8 (.D(d_ff_7_q), .clk(button_4_out), .Q(d_ff_8_q), .reset(button_3_out));  // open: Qn, preset
  xor xor_5 (xor_5_out, d_ff_6_q, d_ff_22_q);
  xor xor_6 (xor_6_out, xor_5_out, or_3_out);
  LED led_10 (.in(xor_6_out));
  LED led_11 (.in(in_6));
  LED led_12 (.in(in_7));
  D_Flip_Flop d_ff_9 (.D(d_ff_10_q), .clk(button_4_out), .Q(d_ff_9_q), .reset(button_3_out));  // open: Qn, preset
  and and_5 (and_5_out, d_ff_8_q, d_ff_24_q);
  LED led_13 (.in(in_8));
  D_Flip_Flop d_ff_10 (.D(in_5), .clk(button_2_out), .Q(d_ff_10_q), .reset(button_3_out));  // open: Qn, preset
  and and_6 (and_6_out, xor_7_out, or_4_out);
  or or_3 (or_3_out, and_5_out, and_6_out);
  D_Flip_Flop d_ff_11 (.D(in_6), .clk(button_2_out), .Q(d_ff_11_q), .reset(button_3_out));  // open: Qn, preset
  D_Flip_Flop d_ff_12 (.D(d_ff_11_q), .clk(button_4_out), .Q(d_ff_12_q), .reset(button_3_out));  // open: Qn, preset
  xor xor_7 (xor_7_out, d_ff_8_q, d_ff_24_q);
  xor xor_8 (xor_8_out, xor_7_out, or_4_out);
  LED led_14 (.in(xor_8_out));
  D_Flip_Flop d_ff_13 (.D(in_7), .clk(button_2_out), .Q(d_ff_13_q), .reset(button_3_out));  // open: Qn, preset
  D_Flip_Flop d_ff_14 (.D(d_ff_13_q), .clk(button_4_out), .Q(d_ff_14_q), .reset(button_3_out));  // open: Qn, preset
  and and_7 (and_7_out, d_ff_9_q, d_ff_25_q);
  or or_4 (or_4_out, and_7_out, and_8_out);
  Button button_6 ();  // open: out
  LED led_15 ();  // open: in
  D_Flip_Flop d_ff_15 (.D(in_8), .clk(button_2_out), .Q(d_ff_15_q), .reset(button_3_out));  // open: Qn, preset
  D_Flip_Flop d_ff_16 (.D(d_ff_15_q), .clk(button_4_out), .Q(d_ff_16_q), .reset(button_3_out));  // open: Qn, preset
  and and_8 (and_8_out, xor_9_out, or_5_out);
  LED led_16 (.in(in_9));
  xor xor_9 (xor_9_out, d_ff_9_q, d_ff_25_q);
  xor xor_10 (xor_10_out, xor_9_out, or_5_out);
  LED led_17 (.in(xor_10_out));
  LED led_18 (.in(in_10));
  D_Flip_Flop d_ff_17 (.D(in_9), .clk(button_2_out), .Q(d_ff_17_q), .reset(button_3_out));  // open: Qn, preset
  D_Flip_Flop d_ff_18 (.D(d_ff_17_q), .clk(button_4_out), .Q(d_ff_18_q), .reset(button_3_out));  // open: Qn, preset
  and and_9 (and_9_out, d_ff_12_q, d_ff_28_q);
  LED led_19 (.in(in_11));
  LED led_20 (.in(in_12));
  D_Flip_Flop d_ff_19 (.D(in_10), .clk(button_2_out), .Q(d_ff_19_q), .reset(button_3_out));  // open: Qn, preset
  D_Flip_Flop d_ff_20 (.D(d_ff_19_q), .clk(button_4_out), .Q(d_ff_20_q), .reset(button_3_out));  // open: Qn, preset
  and and_10 (and_10_out, xor_11_out, or_6_out);
  or or_5 (or_5_out, and_9_out, and_10_out);
  LED led_21 (.in(in_13));
  D_Flip_Flop d_ff_21 (.D(in_11), .clk(button_2_out), .Q(d_ff_21_q), .reset(button_3_out));  // open: Qn, preset
  D_Flip_Flop d_ff_22 (.D(d_ff_21_q), .clk(button_4_out), .Q(d_ff_22_q), .reset(button_3_out));  // open: Qn, preset
  xor xor_11 (xor_11_out, d_ff_12_q, d_ff_28_q);
  xor xor_12 (xor_12_out, xor_11_out, or_6_out);
  LED led_22 (.in(xor_12_out));
  LED led_23 (.in(in_14));
  D_Flip_Flop d_ff_23 (.D(in_12), .clk(button_2_out), .Q(d_ff_23_q), .reset(button_3_out));  // open: Qn, preset
  D_Flip_Flop d_ff_24 (.D(d_ff_23_q), .clk(button_4_out), .Q(d_ff_24_q), .reset(button_3_out));  // open: Qn, preset
  LED led_24 (.in(in_15));
  LED led_25 (.in(in_16));
  D_Flip_Flop d_ff_25 (.D(d_ff_26_q), .clk(button_4_out), .Q(d_ff_25_q), .reset(button_3_out));  // open: Qn, preset
  and and_11 (and_11_out, d_ff_14_q, d_ff_30_q);
  D_Flip_Flop d_ff_26 (.D(in_13), .clk(button_2_out), .Q(d_ff_26_q), .reset(button_3_out));  // open: Qn, preset
  and and_12 (and_12_out, xor_13_out, and_13_out);
  or or_6 (or_6_out, and_11_out, and_12_out);
  D_Flip_Flop d_ff_27 (.D(in_14), .clk(button_2_out), .Q(d_ff_27_q), .reset(button_3_out));  // open: Qn, preset
  D_Flip_Flop d_ff_28 (.D(d_ff_27_q), .clk(button_4_out), .Q(d_ff_28_q), .reset(button_3_out));  // open: Qn, preset
  xor xor_13 (xor_13_out, d_ff_14_q, d_ff_30_q);
  xor xor_14 (xor_14_out, xor_13_out, and_13_out);
  LED led_26 (.in(xor_14_out));
  D_Flip_Flop d_ff_29 (.D(in_15), .clk(button_2_out), .Q(d_ff_29_q), .reset(button_3_out));  // open: Qn, preset
  D_Flip_Flop d_ff_30 (.D(d_ff_29_q), .clk(button_4_out), .Q(d_ff_30_q), .reset(button_3_out));  // open: Qn, preset
  and and_13 (and_13_out, d_ff_16_q, d_ff_32_q);
  D_Flip_Flop d_ff_31 (.D(in_16), .clk(button_2_out), .Q(d_ff_31_q), .reset(button_3_out));  // open: Qn, preset
  D_Flip_Flop d_ff_32 (.D(d_ff_31_q), .clk(button_4_out), .Q(d_ff_32_q), .reset(button_3_out));  // open: Qn, preset
  xor xor_15 (xor_15_out, d_ff_16_q, d_ff_32_q);
  LED led_27 (.in(xor_15_out));

  // Notes on the sheet:
  //   +/-
  //   +/-
  //   Load
  //   Reset 
  //   Add
  //   Subtract
  //   +/-
  //   Input A
  //   8 bit Binary Calculator
  //   Input A Display
  //   +/-
  //   +/-
  //   Input B
  //   Input B Display
endmodule
