// Logisim project stage4finalversion.circ as structural Verilog: 1 circuit, main circuit interface
module \interface  (
  input  in_1,
  input  in_2,
  input  in_3,
  input  in_4,
  input  in_5,
  input  in_6,
  input  in_7,
  input  in_8,
  input  in_9,
  input  in_10,
  input  in_11,
  input  in_12,
  input  in_13,
  input  in_14,
  input  in_15,
  input  in_16,
  input  in_17,
  input  in_18
);

  wire and_1_out, and_2_out, and_3_out, and_4_out, and_5_out, and_6_out, and_7_out, and_8_out, and_9_out,
       and_10_out, and_11_out, and_12_out, and_13_out, and_14_out, and_15_out, and_16_out, and_17_out,
       and_18_out, and_19_out, and_20_out, and_21_out, and_22_out, and_23_out, and_24_out, and_25_out,
       and_26_out, and_27_out, button_1_out, button_2_out, button_3_out, button_4_out, button_5_out,
       button_6_out, d_ff_1_q, d_ff_2_q, d_ff_3_q, d_ff_4_q, d_ff_5_q, d_ff_6_q, d_ff_7_q, d_ff_8_q,
       d_ff_9_q, d_ff_10_q, d_ff_11_q, d_ff_12_q, d_ff_13_q, d_ff_14_q, d_ff_15_q, d_ff_16_q, d_ff_17_q,
       d_ff_18_q, d_ff_19_q, d_ff_20_q, d_ff_21_q, d_ff_22_q, d_ff_23_q, d_ff_24_q, d_ff_25_q, d_ff_26_q,
       d_ff_27_q, d_ff_28_q, d_ff_29_q, d_ff_30_q, d_ff_31_q, d_ff_32_q, d_ff_33_q, d_ff_34_q, d_ff_35_q,
       d_ff_36_q, d_ff_37_q, d_ff_38_q, d_ff_39_q, d_ff_40_q, d_ff_41_q, d_ff_42_q, d_ff_43_q, d_ff_44_q,
       d_ff_45_q, d_ff_46_q, d_ff_47_q, d_ff_48_q, or_1_out, or_2_out, or_3_out, or_4_out, or_5_out,
       or_6_out, or_7_out, or_8_out, or_9_out, or_10_out, or_11_out, or_12_out, or_13_out, or_14_out,
       or_15_out, or_16_out, or_17_out, or_18_out, or_19_out, or_20_out, or_21_out, or_22_out, t_ff_1_q,
       t_ff_2_q, xor_1_out, xor_2_out, xor_3_out, xor_4_out, xor_5_out, xor_6_out, xor_7_out, xor_8_out,
       xor_9_out, xor_10_out, xor_11_out, xor_12_out, xor_13_out, xor_14_out, xor_15_out, xor_16_out,
       xor_17_out, xor_18_out, xor_19_out, xor_20_out, xor_21_out, xor_22_out, xor_23_out, xor_24_out,
       xor_25_out, xor_26_out, xor_27_out, xor_28_out, xor_29_out, xor_30_out, xor_31_out, xor_32_out,
       xor_33_out, xor_34_out, xor_35_out, xor_36_out, xor_37_out, xor_38_out, xor_39_out, xor_40_out,
       xor_41_out, xor_42_out, xor_43_out, xor_44_out, xor_45_out, xor_46_out, xor_47_out;

  Button button_1 (.out(button_1_out));
  LED led_1 (.in(t_ff_1_q));
  LED led_2 ();  // open: in
  T_Flip_Flop t_ff_1 (.T(button_1_out), .clk(button_1_out), .Q(t_ff_1_q));  // open: Qn, reset, preset
  Button button_2 (.out(button_2_out));
  Button button_3 (.out(button_3_out));
  Button button_4 (.out(button_4_out));
  Button button_5 (.out(button_5_out));
  xor xor_1 (xor_1_out, in_11, and_1_out);
  xor xor_2 (xor_2_out, xor_1_out, and_2_out);
  D_Flip_Flop d_ff_1 (.D(d_ff_3_q), .clk(button_4_out), .Q(d_ff_1_q), .reset(button_3_out));  // open: Qn, preset
  D_Flip_Flop d_ff_2 (.D(d_ff_3_q), .clk(button_5_out), .Q(d_ff_2_q), .reset(button_3_out));  // open: Qn, preset
  LED led_3 (.in(xor_6_out));
  and and_1 (and_1_out, in_2, t_ff_1_q);
  LED led_4 (.in(in_11));
  xor xor_3 (xor_3_out, in_12, and_1_out);
  and and_2 (and_2_out, xor_7_out, and_3_out);
  xor xor_4 (xor_4_out, xor_3_out, and_2_out);
  D_Flip_Flop d_ff_3 (.D(xor_2_out), .clk(button_2_out), .Q(d_ff_3_q), .reset(button_3_out));  // open: Qn, preset
  or or_1 (or_1_out, d_ff_2_q, d_ff_1_q);
  xor xor_5 (xor_5_out, or_1_out, or_14_out);
  xor xor_6 (xor_6_out, xor_5_out, or_2_out);
  LED led_5 (.in(xor_6_out));
  LED led_6 (.in(in_12));
  LED led_7 (.in(in_13));
  xor xor_7 (xor_7_out, in_13, and_1_out);
  and and_3 (and_3_out, xor_9_out, and_5_out);
  xor xor_8 (xor_8_out, xor_7_out, and_3_out);
  D_Flip_Flop d_ff_4 (.D(xor_4_out), .clk(button_2_out), .Q(d_ff_4_q), .reset(button_3_out));  // open: Qn, preset
  D_Flip_Flop d_ff_5 (.D(d_ff_4_q), .clk(button_4_out), .Q(d_ff_5_q), .reset(button_3_out));  // open: Qn, preset
  D_Flip_Flop d_ff_6 (.D(d_ff_4_q), .clk(button_5_out), .Q(d_ff_6_q), .reset(button_3_out));  // open: Qn, preset
  and and_4 (and_4_out, or_3_out, or_15_out);
  or or_2 (or_2_out, and_4_out, and_6_out);
  LED led_8 (.in(in_14));
  xor xor_9 (xor_9_out, in_14, and_1_out);
  and and_5 (and_5_out, xor_11_out, and_7_out);
  D_Flip_Flop d_ff_7 (.D(d_ff_9_q), .clk(button_4_out), .Q(d_ff_7_q), .reset(button_3_out));  // open: Qn, preset
  D_Flip_Flop d_ff_8 (.D(d_ff_9_q), .clk(button_5_out), .Q(d_ff_8_q), .reset(button_3_out));  // open: Qn, preset
  or or_3 (or_3_out, d_ff_6_q, d_ff_5_q);
  xor xor_10 (xor_10_out, or_3_out, or_15_out);
  and and_6 (and_6_out, xor_10_out, or_5_out);
  LED led_9 (.in(in_15));
  xor xor_11 (xor_11_out, in_15, and_1_out);
  and and_7 (and_7_out, xor_15_out, and_10_out);
  xor xor_12 (xor_12_out, xor_9_out, and_5_out);
  xor xor_13 (xor_13_out, xor_11_out, and_7_out);
  D_Flip_Flop d_ff_9 (.D(xor_8_out), .clk(button_2_out), .Q(d_ff_9_q), .reset(button_3_out));  // open: Qn, preset
  or or_4 (or_4_out, d_ff_8_q, d_ff_7_q);
  xor xor_14 (xor_14_out, xor_10_out, or_5_out);
  LED led_10 (.in(xor_14_out));
  LED led_11 (.in(in_16));
  LED led_12 (.in(in_17));
  xor xor_15 (xor_15_out, in_16, and_1_out);
  D_Flip_Flop d_ff_10 (.D(xor_12_out), .clk(button_2_out), .Q(d_ff_10_q), .reset(button_3_out));  // open: Qn, preset
  D_Flip_Flop d_ff_11 (.D(d_ff_10_q), .clk(button_4_out), .Q(d_ff_11_q), .reset(button_3_out));  // open: Qn, preset
  D_Flip_Flop d_ff_12 (.D(d_ff_10_q), .clk(button_5_out), .Q(d_ff_12_q), .reset(button_3_out));  // open: Qn, preset
  and and_8 (and_8_out, or_4_out, or_17_out);
  and and_9 (and_9_out, xor_17_out, or_7_out);
  or or_5 (or_5_out, and_8_out, and_9_out);
  LED led_13 (.in(in_18));
  and and_10 (and_10_out, xor_19_out, and_13_out);
  xor xor_16 (xor_16_out, xor_15_out, and_10_out);
  D_Flip_Flop d_ff_13 (.D(xor_13_out), .clk(button_2_out), .Q(d_ff_13_q), .reset(button_3_out));  // open: Qn, preset
  D_Flip_Flop d_ff_14 (.D(d_ff_13_q), .clk(button_4_out), .Q(d_ff_14_q), .reset(button_3_out));  // open: Qn, preset
  or or_6 (or_6_out, d_ff_12_q, d_ff_11_q);
  xor xor_17 (xor_17_out, or_4_out, or_17_out);
  xor xor_18 (xor_18_out, xor_17_out, or_7_out);
  LED led_14 (.in(xor_18_out));
  xor xor_19 (xor_19_out, in_17, and_1_out);
  xor xor_20 (xor_20_out, xor_19_out, and_13_out);
  D_Flip_Flop d_ff_15 (.D(xor_16_out), .clk(button_2_out), .Q(d_ff_15_q), .reset(button_3_out));  // open: Qn, preset
  D_Flip_Flop d_ff_16 (.D(d_ff_15_q), .clk(button_4_out), .Q(d_ff_16_q), .reset(button_3_out));  // open: Qn, preset
  D_Flip_Flop d_ff_17 (.D(d_ff_13_q), .clk(button_5_out), .Q(d_ff_17_q), .reset(button_3_out));  // open: Qn, preset
  and and_11 (and_11_out, or_6_out, or_18_out);
  and and_12 (and_12_out, xor_21_out, or_10_out);
  or or_7 (or_7_out, and_11_out, and_12_out);
  and and_13 (and_13_out, xor_22_out, and_1_out);
  D_Flip_Flop d_ff_18 (.D(xor_20_out), .clk(button_2_out), .Q(d_ff_18_q), .reset(button_3_out));  // open: Qn, preset
  D_Flip_Flop d_ff_19 (.D(d_ff_18_q), .clk(button_4_out), .Q(d_ff_19_q), .reset(button_3_out));  // open: Qn, preset
  D_Flip_Flop d_ff_20 (.D(d_ff_15_q), .clk(button_5_out), .Q(d_ff_20_q), .reset(button_3_out));  // open: Qn, preset
  or or_8 (or_8_out, d_ff_17_q, d_ff_14_q);
  xor xor_21 (xor_21_out, or_6_out, or_18_out);
  LED led_15 (.in(t_ff_2_q));
  xor xor_22 (xor_22_out, in_18, and_1_out);
  xor xor_23 (xor_23_out, xor_22_out, and_1_out);
  or or_9 (or_9_out, d_ff_20_q, d_ff_16_q);
  xor xor_24 (xor_24_out, xor_21_out, or_10_out);
  LED led_16 (.in(xor_24_out));
  T_Flip_Flop t_ff_2 (
    .T(button_6_out), .clk(button_6_out), .Q(t_ff_2_q), .reset(button_3_out), .preset(button_5_out));  // open: Qn
  Button button_6 (.out(button_6_out));
  D_Flip_Flop d_ff_21 (.D(xor_23_out), .clk(button_2_out), .Q(d_ff_21_q), .reset(button_3_out));  // open: Qn, preset
  D_Flip_Flop d_ff_22 (.D(d_ff_21_q), .clk(button_4_out), .Q(d_ff_22_q), .reset(button_3_out));  // open: Qn, preset
  D_Flip_Flop d_ff_23 (.D(d_ff_18_q), .clk(button_5_out), .Q(d_ff_23_q), .reset(button_3_out));  // open: Qn, preset
  and and_14 (and_14_out, or_8_out, or_19_out);
  and and_15 (and_15_out, xor_25_out, or_13_out);
  or or_10 (or_10_out, and_14_out, and_15_out);
  D_Flip_Flop d_ff_24 (.D(xor_28_out), .clk(button_2_out), .Q(d_ff_24_q), .reset(button_3_out));  // open: Qn, preset
  D_Flip_Flop d_ff_25 (.D(d_ff_24_q), .clk(button_4_out), .Q(d_ff_25_q), .reset(button_3_out));  // open: Qn, preset
  or or_11 (or_11_out, d_ff_23_q, d_ff_19_q);
  xor xor_25 (xor_25_out, or_8_out, or_19_out);
  and and_16 (and_16_out, in_1, t_ff_2_q);
  xor xor_26 (xor_26_out, in_3, and_16_out);
  xor xor_27 (xor_27_out, in_4, and_16_out);
  xor xor_28 (xor_28_out, xor_26_out, and_17_out);
  D_Flip_Flop d_ff_26 (.D(xor_31_out), .clk(button_2_out), .Q(d_ff_26_q), .reset(button_3_out));  // open: Qn, preset
  D_Flip_Flop d_ff_27 (.D(d_ff_26_q), .clk(button_4_out), .Q(d_ff_27_q), .reset(button_3_out));  // open: Qn, preset
  D_Flip_Flop d_ff_28 (.D(d_ff_21_q), .clk(button_5_out), .Q(d_ff_28_q), .reset(button_3_out));  // open: Qn, preset
  xor xor_29 (xor_29_out, xor_25_out, or_13_out);
  LED led_17 (.in(xor_29_out));
  LED led_18 (.in(in_3));
  LED led_19 (.in(in_4));
  xor xor_30 (xor_30_out, in_5, and_16_out);
  and and_17 (and_17_out, xor_30_out, and_19_out);
  xor xor_31 (xor_31_out, xor_27_out, and_17_out);
  D_Flip_Flop d_ff_29 (.D(d_ff_24_q), .clk(button_5_out), .Q(d_ff_29_q), .reset(button_3_out));  // open: Qn, preset
  or or_12 (or_12_out, d_ff_28_q, d_ff_22_q);
  and and_18 (and_18_out, or_9_out, or_20_out);
  or or_13 (or_13_out, and_18_out, and_20_out);
  LED led_20 (.in(in_5));
  LED led_21 (.in(in_6));
  and and_19 (and_19_out, xor_33_out, and_21_out);
  xor xor_32 (xor_32_out, xor_30_out, and_19_out);
  D_Flip_Flop d_ff_30 (.D(xor_32_out), .clk(button_2_out), .Q(d_ff_30_q), .reset(button_3_out));  // open: Qn, preset
  D_Flip_Flop d_ff_31 (.D(d_ff_30_q), .clk(button_4_out), .Q(d_ff_31_q), .reset(button_3_out));  // open: Qn, preset
  or or_14 (or_14_out, d_ff_29_q, d_ff_25_q);
  and and_20 (and_20_out, xor_35_out, or_16_out);
  LED led_22 (.in(in_7));
  xor xor_33 (xor_33_out, in_6, and_16_out);
  and and_21 (and_21_out, xor_37_out, and_22_out);
  xor xor_34 (xor_34_out, xor_33_out, and_21_out);
  D_Flip_Flop d_ff_32 (.D(xor_34_out), .clk(button_2_out), .Q(d_ff_32_q), .reset(button_3_out));  // open: Qn, preset
  D_Flip_Flop d_ff_33 (.D(d_ff_32_q), .clk(button_4_out), .Q(d_ff_33_q), .reset(button_3_out));  // open: Qn, preset
  D_Flip_Flop d_ff_34 (.D(d_ff_26_q), .clk(button_5_out), .Q(d_ff_34_q), .reset(button_3_out));  // open: Qn, preset
  xor xor_35 (xor_35_out, or_9_out, or_20_out);
  xor xor_36 (xor_36_out, xor_35_out, or_16_out);
  LED led_23 (.in(xor_36_out));
  LED led_24 (.in(in_8));
  xor xor_37 (xor_37_out, in_7, and_16_out);
  and and_22 (and_22_out, xor_39_out, and_23_out);
  xor xor_38 (xor_38_out, xor_37_out, and_22_out);
  D_Flip_Flop d_ff_35 (.D(xor_38_out), .clk(button_2_out), .Q(d_ff_35_q), .reset(button_3_out));  // open: Qn, preset
  D_Flip_Flop d_ff_36 (.D(d_ff_35_q), .clk(button_4_out), .Q(d_ff_36_q), .reset(button_3_out));  // open: Qn, preset
  D_Flip_Flop d_ff_37 (.D(d_ff_30_q), .clk(button_5_out), .Q(d_ff_37_q), .reset(button_3_out));  // open: Qn, preset
  or or_15 (or_15_out, d_ff_34_q, d_ff_27_q);
  LED led_25 (.in(in_9));
  LED led_26 (.in(in_10));
  xor xor_39 (xor_39_out, in_8, and_16_out);
  and and_23 (and_23_out, xor_41_out, and_26_out);
  xor xor_40 (xor_40_out, xor_39_out, and_23_out);
  D_Flip_Flop d_ff_38 (.D(xor_40_out), .clk(button_2_out), .Q(d_ff_38_q), .reset(button_3_out));  // open: Qn, preset
  D_Flip_Flop d_ff_39 (.D(d_ff_38_q), .clk(button_4_out), .Q(d_ff_39_q), .reset(button_3_out));  // open: Qn, preset
  and and_24 (and_24_out, or_11_out, or_21_out);
  and and_25 (and_25_out, xor_43_out, and_27_out);
  or or_16 (or_16_out, and_24_out, and_25_out);
  xor xor_41 (xor_41_out, in_9, and_16_out);
  D_Flip_Flop d_ff_40 (.D(xor_42_out), .clk(button_2_out), .Q(d_ff_40_q), .reset(button_3_out));  // open: Qn, preset
  D_Flip_Flop d_ff_41 (.D(d_ff_40_q), .clk(button_4_out), .Q(d_ff_41_q), .reset(button_3_out));  // open: Qn, preset
  D_Flip_Flop d_ff_42 (.D(d_ff_32_q), .clk(button_5_out), .Q(d_ff_42_q), .reset(button_3_out));  // open: Qn, preset
  or or_17 (or_17_out, d_ff_37_q, d_ff_31_q);
  and and_26 (and_26_out, xor_45_out, and_16_out);
  xor xor_42 (xor_42_out, xor_41_out, and_26_out);
  or or_18 (or_18_out, d_ff_42_q, d_ff_33_q);
  xor xor_43 (xor_43_out, or_11_out, or_21_out);
  xor xor_44 (xor_44_out, xor_43_out, and_27_out);
  LED led_27 (.in(xor_44_out));
  xor xor_45 (xor_45_out, in_10, and_16_out);
  xor xor_46 (xor_46_out, xor_45_out, and_16_out);
  D_Flip_Flop d_ff_43 (.D(xor_46_out), .clk(button_2_out), .Q(d_ff_43_q), .reset(button_3_out));  // open: Qn, preset
  D_Flip_Flop d_ff_44 (.D(d_ff_43_q), .clk(button_4_out), .Q(d_ff_44_q), .reset(button_3_out));  // open: Qn, preset
  D_Flip_Flop d_ff_45 (.D(d_ff_35_q), .clk(button_5_out), .Q(d_ff_45_q), .reset(button_3_out));  // open: Qn, preset
  and and_27 (and_27_out, or_12_out, or_22_out);
  D_Flip_Flop d_ff_46 (.D(d_ff_38_q), .clk(button_5_out), .Q(d_ff_46_q), .reset(button_3_out));  // open: Qn, preset
  or or_19 (or_19_out, d_ff_45_q, d_ff_36_q);
  xor xor_47 (xor_47_out, or_12_out, or_22_out);
  LED led_28 (.in(xor_47_out));
  or or_20 (or_20_out, d_ff_46_q, d_ff_39_q);
  D_Flip_Flop d_ff_47 (.D(d_ff_40_q), .clk(button_5_out), .Q(d_ff_47_q), .reset(button_3_out));  // open: Qn, preset
  or or_21 (or_21_out, d_ff_47_q, d_ff_41_q);
  D_Flip_Flop d_ff_48 (.D(d_ff_43_q), .clk(button_5_out), .Q(d_ff_48_q), .reset(button_3_out));  // open: Qn, preset
  or or_22 (or_22_out, d_ff_48_q, d_ff_44_q);

  // Notes on the sheet:
  //   +/-
  //   +/-
  //   +/-
  //   Load
  //   Reset 
  //   add
  //   subtracr
  //   +/-
  //   Input A
  //   8 bit Binary Calculator
  //   Input A Display
  //   +/-
  //   +/-
  //   Input A
  //   Input A Display
endmodule
